// Digital circuit backup_pixel_rom.dig as structural Verilog
module backup_pixel_rom (
  input  r_i,
  input  g_i,
  input  b_i,
  input  y,
  input  x,
  input  en,
  input  un,
  output r_o,
  output g_o,
  output b_o
);

  wire and_1_out, and_2_out, and_3_out, and_4_out, and_5_out, and_6_out, and_7_out, and_8_out, and_9_out,
       and_10_out, and_11_out, and_12_out, and_13_out, and_14_out, and_15_out, and_16_out, and_17_out,
       and_18_out, and_19_out, not_1_out, not_2_out, not_3_out, or_1_out, or_2_out, or_3_out, or_4_out,
       or_5_out, or_6_out, rs_ff_as_1_q, rs_ff_as_2_q, rs_ff_as_3_q, rs_ff_as_4_q, rs_ff_as_5_q, rs_ff_as_6_q;

  not not_1 (not_1_out, un);
  and and_1 (and_1_out, x, y);
  and and_2 (and_2_out, un, not_1_out);
  not not_2 (not_2_out, en);
  and and_3 (and_3_out, en, not_2_out);
  and and_4 (and_4_out, and_3_out, and_1_out);
  or or_1 (or_1_out, and_2_out, and_4_out);
  or or_2 (or_2_out, and_2_out, and_4_out);
  or or_3 (or_3_out, and_2_out, and_4_out);
  and and_5 (and_5_out, r_i, and_4_out);
  and and_6 (and_6_out, g_i, and_4_out);
  and and_7 (and_7_out, b_i, and_4_out);
  or or_4 (or_4_out, and_10_out, and_7_out);
  or or_5 (or_5_out, and_8_out, and_5_out);
  or or_6 (or_6_out, and_9_out, and_6_out);
  and and_8 (and_8_out, rs_ff_as_4_q, and_2_out);
  and and_9 (and_9_out, rs_ff_as_5_q, and_2_out);
  and and_10 (and_10_out, rs_ff_as_6_q, and_2_out);
  RS_FF_AS rs_ff_as_1 (.S(or_4_out), .R(or_1_out), .Q(rs_ff_as_1_q));  // open: nQ
  RS_FF_AS rs_ff_as_2 (.S(or_5_out), .R(or_2_out), .Q(rs_ff_as_2_q));  // open: nQ
  RS_FF_AS rs_ff_as_3 (.S(or_6_out), .R(or_3_out), .Q(rs_ff_as_3_q));  // open: nQ
  and and_11 (and_11_out, rs_ff_as_2_q, and_3_out);
  and and_12 (and_12_out, rs_ff_as_3_q, and_3_out);
  and and_13 (and_13_out, rs_ff_as_1_q, and_3_out);
  RS_FF_AS rs_ff_as_4 (.S(and_11_out), .R(and_3_out), .Q(rs_ff_as_4_q));  // open: nQ
  RS_FF_AS rs_ff_as_5 (.S(and_12_out), .R(and_3_out), .Q(rs_ff_as_5_q));  // open: nQ
  RS_FF_AS rs_ff_as_6 (.S(and_13_out), .R(and_3_out), .Q(rs_ff_as_6_q));  // open: nQ
  // RGBLED rgbled_1: pin names not known; wires that end beside it: rs_ff_as_4_q, rs_ff_as_5_q, rs_ff_as_6_q
  not not_3 (not_3_out, and_1_out);
  // RGBLED rgbled_2: pin names not known; wires that end beside it: rs_ff_as_2_q, rs_ff_as_3_q, rs_ff_as_1_q
  and and_14 (and_14_out, r_i, and_1_out);
  and and_15 (and_15_out, rs_ff_as_2_q, not_3_out);
  and and_16 (and_16_out, g_i, and_1_out);
  and and_17 (and_17_out, rs_ff_as_3_q, not_3_out);
  and and_18 (and_18_out, b_i, and_1_out);
  and and_19 (and_19_out, rs_ff_as_1_q, not_3_out);
  or or_7 (r_o, and_14_out, and_15_out);
  or or_8 (g_o, and_16_out, and_17_out);
  or or_9 (b_o, and_18_out, and_19_out);
  // RGBLED rgbled_3: pin names not known; wires that end beside it: r_o, g_o, b_o
endmodule
