// Digital circuit decoder_4bits.dig as structural Verilog
module decoder_4bits (
  input  i_0,
  input  i_1,
  input  i_2,
  input  i_3,
  input  all,
  output o_0,
  output o_1,
  output o_2,
  output o_3,
  output o_4,
  output o_5,
  output o_6,
  output o_7,
  output o_8,
  output o_9,
  output o_10,
  output o_11,
  output o_12,
  output o_13,
  output o_14,
  output o_15
);

  wire and_1_out, and_2_out, and_3_out, and_4_out, and_5_out, and_6_out, and_7_out, and_8_out, and_9_out,
       and_10_out, and_11_out, and_12_out, and_13_out, and_14_out, and_15_out, and_16_out, not_1_out,
       not_2_out, not_3_out, not_4_out;

  not not_1 (not_1_out, i_0);
  not not_2 (not_2_out, i_1);
  not not_3 (not_3_out, i_2);
  not not_4 (not_4_out, i_3);
  and and_1 (and_1_out, not_1_out, not_2_out, not_3_out, not_4_out);
  and and_2 (and_2_out, not_1_out, not_2_out, not_3_out, i_3);
  and and_3 (and_3_out, not_1_out, not_2_out, i_2, not_4_out);
  and and_4 (and_4_out, not_1_out, not_2_out, i_2, i_3);
  and and_5 (and_5_out, not_1_out, i_1, not_3_out, not_4_out);
  and and_6 (and_6_out, not_1_out, i_1, not_3_out, i_3);
  and and_7 (and_7_out, not_1_out, i_1, i_2, not_4_out);
  and and_8 (and_8_out, not_1_out, i_1, i_2, i_3);
  and and_9 (and_9_out, i_0, not_2_out, not_3_out, not_4_out);
  and and_10 (and_10_out, i_0, not_2_out, not_3_out, i_3);
  and and_11 (and_11_out, i_0, not_2_out, i_2, not_4_out);
  and and_12 (and_12_out, i_0, not_2_out, i_2, i_3);
  and and_13 (and_13_out, i_0, i_1, not_3_out, not_4_out);
  and and_14 (and_14_out, i_0, i_1, not_3_out, i_3);
  and and_15 (and_15_out, i_0, i_1, i_2, not_4_out);
  and and_16 (and_16_out, i_0, i_1, i_2, i_3);
  or or_1 (o_0, and_1_out, all);
  or or_2 (o_1, and_2_out, all);
  or or_3 (o_2, and_3_out, all);
  or or_4 (o_3, and_4_out, all);
  or or_5 (o_4, and_5_out, all);
  or or_6 (o_5, and_6_out, all);
  or or_7 (o_6, and_7_out, all);
  or or_8 (o_7, and_8_out, all);
  or or_9 (o_8, and_9_out, all);
  or or_10 (o_9, and_10_out, all);
  or or_11 (o_10, and_11_out, all);
  or or_12 (o_11, and_12_out, all);
  or or_13 (o_12, and_13_out, all);
  or or_14 (o_13, and_14_out, all);
  or or_15 (o_14, and_15_out, all);
  or or_16 (o_15, and_16_out, all);
endmodule
