// Digital circuit updown_button_3bits.dig as structural Verilog
module updown_button_3bits (
  input  plus,
  input  in_2,
  output o_0,
  output o_1,
  output o_2
);

  wire and_1_out, and_2_out, and_3_out, and_4_out, and_5_out, and_6_out, and_7_out, not_1_out, not_2_out,
       or_1_out, or_2_out, t_ff_1_nq, t_ff_1_q, t_ff_2_nq, t_ff_3_nq, xor_1_out, xor_2_out;

  not not_1 (not_1_out, t_ff_1_nq);
  and and_1 (and_1_out, plus, not_1_out);
  and and_2 (and_2_out, in_2, t_ff_1_nq);
  and and_3 (and_3_out, t_ff_1_nq, plus);
  xor xor_1 (xor_1_out, and_1_out, and_2_out);
  xor xor_2 (xor_2_out, and_3_out, in_2);
  T_FF t_ff_1 (.T(1'b1), .C(xor_1_out), .Q(t_ff_1_q), .nQ(t_ff_1_nq));
  not not_2 (not_2_out, xor_2_out);
  T_FF t_ff_2 (.T(1'b1), .C(not_2_out), .Q(o_2), .nQ(t_ff_2_nq));
  and and_4 (and_4_out, t_ff_1_nq, o_2);
  and and_5 (and_5_out, t_ff_2_nq, t_ff_1_q);
  or or_1 (or_1_out, and_4_out, and_5_out);
  T_FF t_ff_3 (.T(or_1_out), .C(not_2_out), .Q(o_1), .nQ(t_ff_3_nq));
  and and_6 (and_6_out, and_4_out, o_1);
  and and_7 (and_7_out, t_ff_3_nq, and_5_out);
  or or_2 (or_2_out, and_6_out, and_7_out);
  T_FF t_ff_4 (.T(or_2_out), .C(not_2_out), .Q(o_0));  // open: nQ
endmodule
